# Fritzing sketch SmartProject (saved by Fritzing 0.9.3b)

parts:
  Composant1 = Arduino Uno (Rev3)
  D1 = Rectifier Diode [part_number=1N4001 package="300 mil [THT]"]
  R1 = Resistor [tolerance=±5% resistance=1M package=THT]
  L1 = Inductor [inductance=10mH package="400 mil [THT]"]
  C2 = Electrolytic Capacitor [capacitance=0.1nF package="100 mil [THT, electrolytic]"]
  R2 = Resistor [tolerance=±5% resistance=3.3k package=THT]
  R3 = Resistor [tolerance=±5% resistance=10k package=THT]
  C3 = Electrolytic Capacitor [capacitance=10nF package="100 mil [THT, electrolytic]"]

nets:
  N1: Composant1.A0, D1.cathode, R1.Pin_0, C2.+
  N2: Composant1.D9_PWM, R3.Pin_1
  N3: Composant1.GND, R1.Pin_1, C2.-, R2.Pin_1
  N4: D1.anode, L1.pin_0, C3.-
  N5: L1.pin_1, R2.Pin_0, R3.Pin_0
  Electrode: C3.+
